# Fritzing sketch bldc1 (saved by Fritzing 0.9.3b)
circuit board: 8.46667cm x 5.64444cm
breadboards: 1

parts:
  R1 = Resistor [tolerance=±5% resistance=330 package=THT]
  LED1 = LED - 5mm [color="Red (633nm)" package="5 mm [THT]"]
  R2 = Resistor [tolerance=±5% resistance=330 package=THT]
  LED2 = LED - 5mm [color="Red (633nm)" package="5 mm [THT]"]
  R3 = Resistor [tolerance=±5% resistance=330 package=THT]
  LED3 = LED - 5mm [color="Red (633nm)" package="5 mm [THT]"]
  DS1809 = IC, DIP package, 8 pins [chip_label=DS1809]
  HallPwr = DC Power [voltage=6.25]
  SynHak1 = Arduino Prototyping Shield
  Q1 = npn-Powertransistor [package="TO220 [THT]"]  # not connected
  Rocker = Trimmer Potentiometer [maximum_resistance=10kΩ package=THT]
  HallSns = female pin header, 3 pins [form="♀ (female)"]

nets:
  N1: R1.Pin_0, LED1.anode
  N2: R1.Pin_1, R2.Pin_1, R3.Pin_1, DS1809.pin8, SynHak1.+5V, Rocker.leg2
  N3: LED1.cathode, SynHak1.D2, HallSns.pin1
  N4: R2.Pin_0, LED2.anode
  N5: LED2.cathode, SynHak1.D3, HallSns.pin2
  N6: R3.Pin_0, LED3.anode
  N7: LED3.cathode, SynHak1.D4, HallSns.pin3
  N8: DS1809.pin1, HallPwr.V+
  N9: DS1809.pin2, SynHak1.D6
  N10: DS1809.pin3, DS1809.pin4, HallPwr.V-
  N11: DS1809.pin5, SynHak1.GND
  PotWpr: DS1809.pin6
  N12: DS1809.pin7, SynHak1.D5
  N13: SynHak1.A0, Rocker.wiper
  N14: SynHak1.N$235, SynHak1.N$251
  GND: Rocker.leg1
